# Fritzing sketch simple-ifttt-pumper (saved by Fritzing 0.9.3b)
circuit board: 8.46667cm x 5.64444cm
breadboards: 1

parts:
  Part2 = Adafruit PowerRelay Feather Wing [part_number="Adafruit #3191"]
  IC1 = Voltage Regulator [package=78xxl]
  Part3 = Soil Moisture Sensor
  Part4 = Photon
  J1 = Piezo Speaker
  Power_plug1 = Power plug
  Part5 = Photon

nets:
  N1: Part2.NC, J1.pin2
  N2: Part2.COM, IC1.IN, Power_plug1.VCC
  N3: Part2.RELAY, Part4.D4, Part5.D4
  3V3: Part2.3.3V, Part4.3V3, Part5.3V3
  GND: Part2.GND, Part4.GND, Part5.GND
  GND_2: IC1.GND, J1.pin1, Power_plug1.GND
  VIN: IC1.OUT, Part4.VIN, Part5.VIN
  N4: Part3.VCC, Part4.A1, Part5.A1
  N5: Part3.SIG, Part4.A2, Part5.A2
  N6: Part3.GND, Part4.A0, Part5.A0
  N7: Part4.A3, Part5.A3
  N8: Part4.A4, Part5.A4
  N9: Part4.A5, Part5.A5
  N10: Part4.DAC, Part5.DAC
  N11: Part4.WKP, Part5.WKP
  N12: Part4.RX, Part5.RX
  N13: Part4.TX, Part5.TX
  N14: Part4.D0, Part5.D0
  N15: Part4.D1, Part5.D1
  N16: Part4.D2, Part5.D2
  N17: Part4.D3, Part5.D3
  N18: Part4.D5, Part5.D5
  N19: Part4.D6, Part5.D6
  N20: Part4.D7, Part5.D7
  N21: Part4.VBAT, Part5.VBAT
  N22: Part4.RST, Part5.RST

notes:
  12v Peristaltic Dosing PUmp
  5v rail
  12v rail

custom parts:
  Adafruit PowerRelay Feather Wing: A Feather board without ambition is a Feather board without FeatherWings! This is the Power Relay FeatherWing. It gives you power to control, and control over power. Put simply, you can now turn on and off lamps, fans, solenoids, and other small appliances that run on up to 250VAC or DC power using any Feather board. Compared to our smaller Relay FeatherWings, this one can handle a beefy 1200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
