# Fritzing sketch simple-ifttt-pumper (saved by Fritzing 0.9.3b)
circuit board: 8.46667cm x 5.64444cm
breadboards: 1

parts:
  Part2 = Adafruit PowerRelay Feather Wing [part_number="Adafruit #3191"]
  IC1 = Voltage Regulator [package=78xxl]
  Part3 = Soil Moisture Sensor
  Part4 = Photon
  J1 = Piezo Speaker
  Power_plug1 = Power plug

nets:
  N1: Part2.NC, J1.pin2
  N2: Part2.COM, IC1.IN, Power_plug1.VCC
  N3: Part2.RELAY, Part4.D4
  3.3V: Part2.3.3V, Part4.3V3
  GND: Part2.GND, Part4.GND
  N4: Part2.SCL, IC1.OUT, Part4.VIN
  GND_2: IC1.GND, J1.pin1, Power_plug1.GND
  N5: Part3.SIG, Part4.A2
  N6: Part3.GND, Part4.A0
  N7: Part3.VCC, Part4.A1

notes:
  12v Peristaltic Dosing PUmp
  5v rail
  12v rail

custom parts:
  Adafruit PowerRelay Feather Wing: A Feather board without ambition is a Feather board without FeatherWings! This is the Power Relay FeatherWing. It gives you power to control, and control over power. Put simply, you can now turn on and off lamps, fans, solenoids, and other small appliances that run on up to 250VAC or DC power using any Feather board. Compared to our smaller Relay FeatherWings, this one can handle a beefy 1200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
